// Digital circuit processor.dig as structural Verilog
module processor (
  input  clk
);

  wire undriven, undriven_3, undriven_5, undriven_6;
  wire [1:0] undriven_2;
  wire [2:0] undriven_4;
  wire [15:0] add_1_s, add_2_s, multiplexer_1_out, PC_q;
  wire [31:0] code_memory_d, immediatetransformer_1_output, multiplexer_2_out, multiplexer_3_out,
       ramdualport_1_d, registrador_1_a, registrador_1_b, ula_1_output;

  Multiplexer #(.Bits(16)) multiplexer_1 (.sel(undriven_6), .in_0(add_1_s), .in_1(add_2_s), .out(multiplexer_1_out));
  D_FF #(.Bits(16)) PC (.D(multiplexer_1_out), .C(clk), .Q(PC_q));  // open: nQ
  Add #(.Bits(16)) add_1 (.a(16'h4), .b(PC_q), .c_i(1'b0), .s(add_1_s));  // open: c_o
  ROM #(.AddrBits(16), .Bits(32)) code_memory (.A(PC_q), .sel(1'b1), .D(code_memory_d));
  registrador registrador_1 (
    .rs1(code_memory_d[19:15]), .rs2(code_memory_d[24:20]), .rd(code_memory_d[11:7]),
    .ula(multiplexer_3_out), .W_reg(undriven), .A(registrador_1_a), .B(registrador_1_b));  // open: ck
  immediateTransformer immediatetransformer_1 (
    .\output (immediatetransformer_1_output), .ImmSelec(undriven_2), .A(code_memory_d));
  Multiplexer #(.Bits(32)) multiplexer_2 (
    .sel(undriven_3), .in_0(registrador_1_b), .in_1(immediatetransformer_1_output), .out(multiplexer_2_out));
  Add #(.Bits(16)) add_2 (.a(PC_q), .b(immediatetransformer_1_output[15:0]), .c_i(1'b0), .s(add_2_s));  // open: c_o
  ula ula_1 (.A(registrador_1_a), .B(multiplexer_2_out), .Output(ula_1_output), .c_ula(undriven_4));  // open: zero
  RAMDualPort #(.AddrBits(24), .Bits(32)) ramdualport_1 (
    .A(ula_1_output[23:0]), .Din(registrador_1_b), .D(ramdualport_1_d));  // open: str, C, ld
  Multiplexer #(.Bits(32)) multiplexer_3 (
    .sel(undriven_5), .in_0(ula_1_output), .in_1(ramdualport_1_d), .out(multiplexer_3_out));
  // Pins of 24 and 32 bits meet at ula_1_output

  // Notes on the sheet:
  //   contents of code_memory (hex, n*v repeats v):
  //   2,0,0,0,3,0,0,0,4,0,0,0,5
endmodule
